// Logisim project simulador1_1 (1).circ as structural Verilog: 10 circuits, main circuit main
module main (
  input  a3,
  input  a2,
  input  a1,
  input  a0,
  input  b0,
  input  b1,
  input  b2,
  input  b3
);

  wire meu_decodificador_1_a, meu_decodificador_1_b, meu_decodificador_1_c, meu_decodificador_1_d,
       meu_decodificador_1_e, meu_decodificador_1_f, meu_decodificador_1_g, meu_decodificador_2_a,
       meu_decodificador_2_b, meu_decodificador_2_c, meu_decodificador_2_d, meu_decodificador_2_e,
       meu_decodificador_2_f, meu_decodificador_2_g, meu_decodificador_3_a, meu_decodificador_3_b,
       meu_decodificador_3_c, meu_decodificador_3_d, meu_decodificador_3_e, meu_decodificador_3_f,
       meu_decodificador_3_g, somador_4_bits_1_soma_0, somador_4_bits_1_soma_1, somador_4_bits_1_soma_2,
       somador_4_bits_1_soma_3;

  meu_decodificador meu_decodificador_1 (
    .S1(a0), .S2(a1), .S3(a2), .S4(a3), .a(meu_decodificador_1_a), .b(meu_decodificador_1_b),
    .c(meu_decodificador_1_c), .d(meu_decodificador_1_d), .e(meu_decodificador_1_e),
    .f(meu_decodificador_1_f), .g(meu_decodificador_1_g));
  Somador_4_bits somador_4_bits_1 (
    .a0(a0), .a1(a1), .a2(a2), .a3(a3), .b0(b0), .b1(b1), .b2(b2), .b3(b3), .Soma_0(somador_4_bits_1_soma_0),
    .Soma_1(somador_4_bits_1_soma_1), .Soma_2(somador_4_bits_1_soma_2), .Soma_3(somador_4_bits_1_soma_3));  // open: Overflow
  meu_decodificador meu_decodificador_2 (
    .S1(b0), .S2(b1), .S3(b2), .S4(b3), .a(meu_decodificador_2_a), .b(meu_decodificador_2_b),
    .c(meu_decodificador_2_c), .d(meu_decodificador_2_d), .e(meu_decodificador_2_e),
    .f(meu_decodificador_2_f), .g(meu_decodificador_2_g));
  _7_Segment_Display u_7_segment_display_1 (
    .g(meu_decodificador_1_g), .f(meu_decodificador_1_f), .a(meu_decodificador_1_a),
    .b(meu_decodificador_1_b), .e(meu_decodificador_1_c), .d(meu_decodificador_1_d));  // open: c, dp
  meu_decodificador meu_decodificador_3 (
    .S1(somador_4_bits_1_soma_0), .S2(somador_4_bits_1_soma_1), .S3(somador_4_bits_1_soma_2),
    .S4(somador_4_bits_1_soma_3), .a(meu_decodificador_3_a), .b(meu_decodificador_3_b),
    .c(meu_decodificador_3_c), .d(meu_decodificador_3_d), .e(meu_decodificador_3_e),
    .f(meu_decodificador_3_f), .g(meu_decodificador_3_g));
  _7_Segment_Display u_7_segment_display_2 (
    .g(meu_decodificador_2_g), .f(meu_decodificador_2_f), .a(meu_decodificador_2_a),
    .b(meu_decodificador_2_b), .e(meu_decodificador_2_e), .d(meu_decodificador_2_d), .c(meu_decodificador_2_c));  // open: dp
  _7_Segment_Display u_7_segment_display_3 (
    .g(meu_decodificador_3_f), .f(meu_decodificador_3_g), .a(meu_decodificador_3_a),
    .b(meu_decodificador_3_b), .e(meu_decodificador_3_e), .d(meu_decodificador_3_d), .c(meu_decodificador_3_c));  // open: dp
endmodule

module meu_decodificador (
  input  S1,
  input  S2,
  input  S3,
  input  S4,
  output a,
  output b,
  output c,
  output d,
  output e,
  output f,
  output g
);

  wire and_1_out, and_2_out, and_3_out, and_4_out, and_5_out, and_6_out, and_7_out, and_8_out, and_9_out,
       and_10_out, and_11_out, and_12_out, and_13_out, and_14_out, and_15_out, and_16_out, and_17_out,
       and_18_out, and_19_out, and_20_out, and_21_out, and_22_out, and_23_out, and_24_out, and_25_out,
       and_26_out, and_27_out, and_28_out, and_29_out, and_30_out, and_31_out, and_32_out, and_33_out,
       and_34_out, and_35_out, and_36_out, not_1_out, not_2_out, not_3_out, not_4_out, not_5_out, not_6_out,
       not_7_out, not_8_out, not_9_out, not_10_out, not_11_out, not_12_out, not_13_out, not_14_out,
       not_15_out, not_16_out, not_17_out, not_18_out, not_19_out, not_20_out, not_21_out, not_22_out,
       not_23_out, not_24_out, not_25_out, not_26_out, not_27_out, not_28_out, not_29_out, not_30_out,
       not_31_out, not_32_out, not_33_out, not_34_out, not_35_out, not_36_out, not_37_out, not_38_out,
       not_39_out, not_40_out, not_41_out, not_42_out, not_43_out, not_44_out, not_45_out;

  not not_1 (not_1_out, S2);
  and and_1 (and_1_out, not_1_out, not_2_out);
  not not_2 (not_2_out, S4);
  not not_3 (not_3_out, S1);
  and and_2 (and_2_out, not_3_out, S3);
  not not_4 (not_4_out, S1);
  and and_3 (and_3_out, not_4_out, S2, S4);
  and and_4 (and_4_out, S2, S3);
  and and_5 (and_5_out, S1, not_5_out, not_6_out);
  not not_5 (not_5_out, S2);
  not not_6 (not_6_out, S3);
  and and_6 (and_6_out, S1, not_7_out);
  not not_7 (not_7_out, S4);
  not not_8 (not_8_out, S1);
  and and_7 (and_7_out, not_8_out, not_9_out);
  not not_9 (not_9_out, S2);
  not not_10 (not_10_out, S1);
  not not_11 (not_11_out, S3);
  and and_8 (and_8_out, not_10_out, not_11_out, not_12_out);
  not not_12 (not_12_out, S4);
  not not_13 (not_13_out, S2);
  and and_9 (and_9_out, not_13_out, not_14_out);
  not not_14 (not_14_out, S3);
  not not_15 (not_15_out, S2);
  and and_10 (and_10_out, not_15_out, not_16_out);
  not not_16 (not_16_out, S4);
  not not_17 (not_17_out, S1);
  and and_11 (and_11_out, not_17_out, S3, S4);
  and and_12 (and_12_out, S1, not_18_out, S4);
  not not_18 (not_18_out, S3);
  not not_19 (not_19_out, S1);
  and and_13 (and_13_out, not_19_out, not_20_out);
  not not_20 (not_20_out, S3);
  not not_21 (not_21_out, S1);
  and and_14 (and_14_out, not_21_out, S4);
  not not_22 (not_22_out, S3);
  and and_15 (and_15_out, not_22_out, S4);
  not not_23 (not_23_out, S1);
  and and_16 (and_16_out, not_23_out, S2);
  and and_17 (and_17_out, S1, not_24_out);
  not not_24 (not_24_out, S2);
  not not_25 (not_25_out, S1);
  not not_26 (not_26_out, S2);
  and and_18 (and_18_out, not_25_out, not_26_out, not_27_out);
  not not_27 (not_27_out, S4);
  not not_28 (not_28_out, S2);
  and and_19 (and_19_out, not_28_out, S3, S4);
  and and_20 (and_20_out, S2, not_29_out, S4);
  not not_29 (not_29_out, S3);
  and and_21 (and_21_out, S2, S3, not_30_out);
  not not_30 (not_30_out, S4);
  and and_22 (and_22_out, S1, not_31_out);
  not not_31 (not_31_out, S3);
  not not_32 (not_32_out, S2);
  and and_23 (and_23_out, not_32_out, not_33_out);
  not not_33 (not_33_out, S4);
  and and_24 (and_24_out, S3, not_34_out);
  not not_34 (not_34_out, S4);
  and and_25 (and_25_out, S1, S3);
  and and_26 (and_26_out, S1, S2);
  not not_35 (not_35_out, S3);
  and and_27 (and_27_out, not_35_out, not_36_out);
  not not_36 (not_36_out, S4);
  not not_37 (not_37_out, S1);
  and and_28 (and_28_out, not_37_out, S2, not_38_out);
  not not_38 (not_38_out, S3);
  and and_29 (and_29_out, S2, not_39_out);
  not not_39 (not_39_out, S4);
  and and_30 (and_30_out, S1, not_40_out);
  not not_40 (not_40_out, S2);
  and and_31 (and_31_out, S1, S3);
  not not_41 (not_41_out, S2);
  and and_32 (and_32_out, not_41_out, S3);
  and and_33 (and_33_out, S3, not_42_out);
  not not_42 (not_42_out, S4);
  not not_43 (not_43_out, S1);
  and and_34 (and_34_out, not_43_out, S2, not_44_out);
  not not_44 (not_44_out, S3);
  and and_35 (and_35_out, S1, not_45_out);
  not not_45 (not_45_out, S2);
  and and_36 (and_36_out, S1, S4);
  or or_1 (c, and_13_out, and_14_out, and_15_out, and_16_out, and_17_out);
  or or_2 (d, and_18_out, and_19_out, and_20_out, and_21_out, and_22_out);
  or or_3 (e, and_23_out, and_24_out, and_25_out, and_26_out);
  or or_4 (f, and_27_out, and_28_out, and_29_out, and_30_out, and_31_out);
  or or_5 (g, and_32_out, and_33_out, and_34_out, and_35_out, and_36_out);
  or or_6 (a, and_1_out, and_2_out, and_3_out, and_4_out, and_5_out, and_6_out);
  or or_7 (b, and_7_out, and_8_out, and_9_out, and_10_out, and_11_out, and_12_out);
endmodule

module Meio_Somador (
  input  a,
  input  b,
  output Meio_Soma,
  output Meio_Vai1
);

  xor xor_1 (Meio_Soma, a, b);
  and and_1 (Meio_Vai1, a, b);
endmodule

module Somador_1_Bit (
  input  Vem_1,
  input  a,
  input  b,
  output Soma_1bit,
  output Vai_1
);

  wire meio_somador_1_meio_soma, meio_somador_1_meio_vai1, meio_somador_2_meio_vai1;

  Meio_Somador meio_somador_1 (
    .a(a), .b(b), .Meio_Soma(meio_somador_1_meio_soma), .Meio_Vai1(meio_somador_1_meio_vai1));
  Meio_Somador meio_somador_2 (
    .a(Vem_1), .b(meio_somador_1_meio_soma), .Meio_Soma(Soma_1bit), .Meio_Vai1(meio_somador_2_meio_vai1));
  or or_1 (Vai_1, meio_somador_2_meio_vai1, meio_somador_1_meio_vai1);
endmodule

module Somador_4_bits (
  input  a0,
  input  a1,
  input  a2,
  input  a3,
  input  b0,
  input  b1,
  input  b2,
  input  b3,
  output Soma_0,
  output Soma_1,
  output Soma_2,
  output Soma_3,
  output Overflow
);

  wire somador_1_bit_1_vai_1, somador_1_bit_2_vai_1, somador_1_bit_3_vai_1, somador_1_bit_4_vai_1;

  Somador_1_Bit somador_1_bit_1 (.Vem_1(1'b0), .a(a0), .b(b0), .Soma_1bit(Soma_0), .Vai_1(somador_1_bit_1_vai_1));
  Somador_1_Bit somador_1_bit_2 (
    .Vem_1(somador_1_bit_1_vai_1), .a(a1), .b(b1), .Soma_1bit(Soma_1), .Vai_1(somador_1_bit_2_vai_1));
  Somador_1_Bit somador_1_bit_3 (
    .Vem_1(somador_1_bit_2_vai_1), .a(a2), .b(b2), .Soma_1bit(Soma_2), .Vai_1(somador_1_bit_3_vai_1));
  Somador_1_Bit somador_1_bit_4 (
    .Vem_1(somador_1_bit_3_vai_1), .a(a3), .b(b3), .Soma_1bit(Soma_3), .Vai_1(somador_1_bit_4_vai_1));
  xor xor_1 (Overflow, somador_1_bit_3_vai_1, somador_1_bit_4_vai_1);
endmodule

module ALU_1bit (
  input  Binverte,
  input  CIN,
  input  A,
  input  B,
  input  Op1,
  input  Op0,
  output out_7,
  output Count
);

  wire and_1_out, Mux2_out_4, not_1_out, not_2_out, or_1_out, Somador_soma_1bit;

  not not_1 (not_1_out, B);
  mux2 Mux2 (.in_1(B), .in_2(not_1_out), .in_3(Binverte), .out_4(Mux2_out_4));
  and and_1 (and_1_out, A, B);
  or or_1 (or_1_out, A, B);
  not not_2 (not_2_out, A);
  Somador_1_Bit Somador (.Vem_1(CIN), .a(A), .b(Mux2_out_4), .Soma_1bit(Somador_soma_1bit), .Vai_1(Count));
  mux4 Mux4 (
    .in_1(and_1_out), .in_2(or_1_out), .in_3(not_2_out), .in_4(Somador_soma_1bit), .in_5(Op1), .in_6(Op0),
    .out_7(out_7));
endmodule

module mux4 (
  input  in_1,
  input  in_2,
  input  in_3,
  input  in_4,
  input  in_5,
  input  in_6,
  output out_7
);

  wire and_1_out, and_2_out, and_3_out, and_4_out, not_1_out, not_2_out, not_3_out, not_4_out;

  and and_1 (and_1_out, in_1, not_1_out, not_2_out);
  not not_1 (not_1_out, in_5);
  not not_2 (not_2_out, in_6);
  not not_3 (not_3_out, in_5);
  and and_2 (and_2_out, in_2, not_3_out, in_6);
  and and_3 (and_3_out, in_3, in_5, not_4_out);
  not not_4 (not_4_out, in_6);
  and and_4 (and_4_out, in_4, in_5, in_6);
  or or_1 (out_7, and_1_out, and_2_out, and_3_out, and_4_out);
endmodule

module mux2 (
  input  in_1,
  input  in_2,
  input  in_3,
  output out_4
);

  wire and_1_out, and_2_out, not_1_out;

  not not_1 (not_1_out, in_3);
  and and_1 (and_1_out, in_1, not_1_out);
  and and_2 (and_2_out, in_2, in_3);
  or or_1 (out_4, and_1_out, and_2_out);
endmodule

module ALU_4bit (
  input  BInverte,
  input  A0,
  input  A1,
  input  A2,
  input  A3,
  input  B0,
  input  B1,
  input  B2,
  input  B3,
  input  OP0,
  input  OP1,
  output S0,
  output S1,
  output S2,
  output S3,
  output Cout
);

  wire alu_1bit_1_count, alu_1bit_2_count, alu_1bit_3_count;

  ALU_1bit alu_1bit_1 (
    .Binverte(BInverte), .CIN(BInverte), .A(A0), .B(B0), .Op1(OP1), .Op0(OP0), .Count(alu_1bit_1_count),
    .out_7(S0));
  ALU_1bit alu_1bit_2 (
    .Binverte(BInverte), .CIN(alu_1bit_1_count), .A(A1), .B(B1), .Op1(OP1), .Op0(OP0),
    .Count(alu_1bit_2_count), .out_7(S1));
  ALU_1bit alu_1bit_3 (
    .Binverte(BInverte), .CIN(alu_1bit_2_count), .A(A2), .B(B2), .Op1(OP1), .Op0(OP0),
    .Count(alu_1bit_3_count), .out_7(S2));
  ALU_1bit alu_1bit_4 (
    .Binverte(BInverte), .CIN(alu_1bit_3_count), .A(A3), .B(B3), .Op1(OP1), .Op0(OP0), .Count(Cout),
    .out_7(S3));
endmodule

module ULA_4BITS (
  input  [3:0] A,
  input  [3:0] B,
  input  [3:0] in_3,
  output [3:0] out_4
);

  wire [3:0] and_1_out, and_2_out, and_3_out, nand_1_out, nor_1_out, not_1_out, not_2_out, not_3_out,
       not_4_out, not_5_out, not_6_out, or_1_out, or_2_out, or_3_out, xor_1_out;

  assign not_1_out = ~A;  // NOT_Gate not_1, 4 bits wide
  assign nor_1_out = ~(A | B);  // NOR_Gate nor_1, 4 bits wide
  assign not_2_out = ~B;  // NOT_Gate not_2, 4 bits wide
  assign not_3_out = ~A;  // NOT_Gate not_3, 4 bits wide
  assign not_4_out = ~B;  // NOT_Gate not_4, 4 bits wide
  assign and_1_out = not_1_out & B;  // AND_Gate and_1, 4 bits wide
  assign nand_1_out = ~(A & B);  // NAND_Gate nand_1, 4 bits wide
  assign xor_1_out = A ^ B;  // XOR_Gate xor_1, 4 bits wide
  assign and_2_out = A & not_2_out;  // AND_Gate and_2, 4 bits wide
  assign or_1_out = not_3_out | B;  // OR_Gate or_1, 4 bits wide
  assign and_3_out = A & B;  // AND_Gate and_3, 4 bits wide
  assign or_2_out = A | not_4_out;  // OR_Gate or_2, 4 bits wide
  assign or_3_out = A | B;  // OR_Gate or_3, 4 bits wide
  assign not_5_out = ~B;  // NOT_Gate not_5, 4 bits wide
  assign not_6_out = ~xor_1_out;  // NOT_Gate not_6, 4 bits wide
  Multiplexer #(.select(4), .width(4)) multiplexer_1 (
    .in0(not_1_out), .in1(nor_1_out), .in2(and_1_out), .in3(4'b0000), .in4(nand_1_out), .in5(not_5_out),
    .in6(xor_1_out), .in7(and_2_out), .in8(or_1_out), .in9(not_6_out), .in10(B), .in11(and_3_out),
    .in12(4'b1111), .in13(or_2_out), .in14(or_3_out), .in15(A), .out(out_4), .sel(in_3));  // open: en
endmodule
